# Fritzing sketch hub (saved by Fritzing 0.7.10b)
breadboards: 1

parts:
  Q1 = NPN-Transistor [package="TO92 [THT]"]  # not connected
  Součástka2 = Barometric Pressure Sensor - BMP085 Breakout
  J4 = Generic male header - 10 pins [package=THT]
  J5 = Generic male header - 10 pins [package=THT]
  J6 = Generic male header - 10 pins [package=THT]
  J7 = Generic male header - 4 pins [package=THT]
  J8 = Generic male header - 4 pins [package=THT]
  Arduino_Mini_Pro1 = Arduino Mini Pro
  R1 = Resistor [tolerance=±5% resistance=220 package=THT]
  Součástka3 = Tri-Axis Gyro Breakout - L3G4200D  # not connected

nets:
  N1: Součástka2.SCL, J7.pin1, J8.pin1, Arduino_Mini_Pro1.A5
  N2: Součástka2.SDA, J7.pin2, J8.pin2, Arduino_Mini_Pro1.A4
  N3: J4.pin1, J4.pin2, J4.pin3, J4.pin4, J4.pin5, J4.pin6, J4.pin7, J4.pin8, J4.pin9, J4.pin10, J7.pin3, J8.pin3, Arduino_Mini_Pro1.VCC, R1.Pin_1
  N4: J5.pin1, J5.pin2, J5.pin3, J5.pin4, J5.pin5, J5.pin6, J5.pin7, J5.pin8, J5.pin9, J5.pin10, J7.pin4, J8.pin4, Arduino_Mini_Pro1.GND
  N5: J6.pin1, Arduino_Mini_Pro1.D1
  N6: J6.pin2, J6.pin3, Arduino_Mini_Pro1.D2, R1.Pin_0
  N7: J6.pin4, J6.pin5, Arduino_Mini_Pro1.D4
  N8: J6.pin6, Arduino_Mini_Pro1.D5
  N9: J6.pin7, Arduino_Mini_Pro1.D6
  N10: J6.pin8, Arduino_Mini_Pro1.D7
